// Logisim project sap2.circ as structural Verilog
module main (
  input  in_1,
  input  in_2,
  input  in_3,
  input  [1:0] in_4,
  output out_5,
  output out_6,
  output out_7,
  output out_8,
  output out_9,
  output out_10,
  output out_11,
  output out_12,
  output out_13,
  output [7:0] out_14,
  output [15:0] out_15,
  output [7:0] out_16,
  output out_17,
  output out_18,
  output out_19,
  output out_20,
  output out_21,
  output out_22,
  output out_23,
  output out_24,
  output out_25,
  output out_26,
  output out_27,
  output out_28,
  output [11:0] out_29
);

  wire and_1_out, and_4_out, and_5_out, clock_1_out, comparator_1_eq, controlled_buffer_6_out,
       controlled_buffer_7_out, counter_1_carry, counter_4_carry, not_1_out, not_2_out, not_3_out, not_4_out,
       not_5_out, not_6_out, not_7_out, not_8_out;
  wire [2:0] counter_2_q;
  wire [3:0] counter_1_q, counter_3_q, register_1_q, rom_2_data;
  wire [7:0] adder_1_out, and_2_out, and_3_out, or_1_out, register_2_q, register_3_q, register_4_q;
  wire [11:0] rom_1_data;

  Clock clock_1 (.out(clock_1_out));
  and and_1 (and_1_out, ~counter_1_carry, clock_1_out);  // AND_Gate
  not not_1 (not_1_out, out_19);
  not not_2 (not_2_out, out_20);
  not not_3 (not_3_out, out_21);
  Counter #(.max('hf), .width(4)) counter_1 (
    .count(out_17), .clk(and_1_out), .carry(counter_1_carry), .Q(counter_1_q));  // open: clr, load, up, D
  RAM #(.addrWidth(4), .trigger("falling"), .\type ("nonvolatile")) ram_1 (
    .addr(register_1_q), .oe(in_3), .clk(and_1_out), .dout(out_14));  // open: we, din
  not not_4 (not_4_out, out_22);
  Register #(.width(4)) register_1 (
    .D({out_9, out_10, out_11, out_12}), .en(not_1_out), .clk(and_1_out), .Q(register_1_q));  // open: clr
  Register register_2 (
    .D({out_5, out_6, out_7, out_8, out_9, out_10, out_11, out_12}), .en(not_3_out), .clk(and_1_out),
    .Q(register_2_q));  // open: clr
  assign {out_9, out_10, out_11, out_12} = out_18 ? counter_1_q : 4'bz;  // Controlled_Buffer controlled_buffer_1
  assign {out_5, out_6, out_7, out_8, out_9, out_10, out_11, out_12} = not_4_out ? register_2_q : 8'bz;  // Controlled_Buffer controlled_buffer_2
  assign {out_5, out_6, out_7, out_8, out_9, out_10, out_11, out_12} = not_2_out ? out_14 : 8'bz;  // Controlled_Buffer controlled_buffer_3
  ROM #(.addrWidth(2), .dataWidth(12)) rom_1 (.addr(in_4), .data(rom_1_data));
  assign {out_5, out_6, out_7, out_8, out_9, out_10, out_11, out_12} = out_24 ? register_3_q : 8'bz;  // Controlled_Buffer controlled_buffer_4
  assign {out_5, out_6, out_7, out_8, out_9, out_10, out_11, out_12} = out_26 ? adder_1_out : 8'bz;  // Controlled_Buffer controlled_buffer_5
  Register register_3 (
    .D({out_5, out_6, out_7, out_8, out_9, out_10, out_11, out_12}), .en(not_7_out), .clk(and_1_out),
    .Q(register_3_q));  // open: clr
  assign or_1_out = and_2_out | and_3_out;  // OR_Gate or_1, 8 bits wide
  assign and_2_out = register_4_q & ~{8{out_25}};  // AND_Gate and_2, 8 bits wide
  Register register_4 (
    .D({out_5, out_6, out_7, out_8, out_9, out_10, out_11, out_12}), .en(not_8_out), .clk(and_1_out),
    .Q(register_4_q));  // open: clr
  Register register_5 (
    .D({out_5, out_6, out_7, out_8, out_9, out_10, out_11, out_12}), .en(not_6_out), .clk(and_1_out),
    .Q(out_16));  // open: clr
  Adder adder_1 (.a(register_3_q), .b(or_1_out), .out(adder_1_out), .cin(out_25));  // open: cout
  assign and_3_out = ~register_4_q & {8{out_25}};  // AND_Gate and_3, 8 bits wide
  ROM #(.addrWidth(4), .dataWidth(4)) rom_2 (.addr(register_2_q[7:4]), .data(rom_2_data));
  Hex_Digit_Display hex_digit_display_1 (.value(out_16[7:4]));  // open: dp
  Hex_Digit_Display hex_digit_display_2 (.value(out_16[3:0]));  // open: dp
  Counter #(.max('h5), .width(3)) counter_2 (.clk(and_1_out), .Q(counter_2_q));  // open: clr, load, up, count, D, carry
  not not_5 (not_5_out, counter_2_q[2]);
  and and_4 (and_4_out, ~counter_2_q[0], ~counter_2_q[1], ~counter_2_q[2]);  // AND_Gate
  Comparator #(.width(12)) comparator_1 (
    .a(rom_1_data),
    .b({out_17, out_18, out_19, out_20, out_21, out_22, out_23, out_24, out_25, out_26, out_27, out_28}),
    .eq(comparator_1_eq));  // open: gt, lt
  not not_6 (not_6_out, out_28);
  and and_5 (and_5_out, counter_2_q[0], counter_2_q[1], not_5_out);
  assign controlled_buffer_6_out = and_1_out ? and_4_out : 1'bz;  // Controlled_Buffer controlled_buffer_6
  not not_7 (not_7_out, out_23);
  Counter #(.max('hf), .trigger("falling"), .width(4)) counter_3 (
    .clr(controlled_buffer_6_out), .load(controlled_buffer_7_out), .clk(and_1_out), .D(rom_2_data),
    .Q(counter_3_q));  // open: up, count, carry
  assign controlled_buffer_7_out = and_1_out ? and_5_out : 1'bz;  // Controlled_Buffer controlled_buffer_7
  ROM #(.addrWidth(4), .dataWidth(12)) rom_3 (
    .addr(counter_3_q),
    .data({out_17, out_18, out_19, out_20, out_21, out_22, out_23, out_24, out_25, out_26, out_27, out_28}));
  not not_8 (not_8_out, out_27);
  RAM #(.addrWidth(16)) ram_2 ();  // open: addr, we, oe, clk, din, dout
  Counter #(.max('hffff), .width(16)) counter_4 (
    .clk(and_1_out), .carry(counter_4_carry), .Q(out_15));  // open: clr, load, up, count, D
  dummy dummy_1 (.in_1(in_1), .in_2(in_2), .out_3(out_13));

  assign out_29 = {out_17, out_18, out_19, out_20, out_21, out_22, out_23, out_24, out_25, out_26, out_27, out_28};

  // Notes on the sheet:
  //   in_3: initial=0x1
  //   Cp
  //   Ep
  //   Lm^
  //   CE^
  //   Li^
  //   Ei^
  //   CpEpLm.CE. 
  //   Eu
  //   Lb^
  //   Lo^
  //   La^
  //   Ea
  //   Su
  //   Li.Ei.La.Ea
  //   SuEuLb.Lo.
  //   contents of rom_1 (hex, n*v repeats v):
  //   3e3
  //   contents of rom_2 (hex, n*v repeats v):
  //   3 6 9 11*0 c
  //   Instruction Bits
  //   contents of rom_3 (hex, n*v repeats v):
  //   5e3 be3 263 1a3 2c3 3e3 1a3 2e1 3c7 1a3 2e1 3cf 3f2 3e3 3e3 3e3
endmodule

module dummy (
  input  in_1,
  input  in_2,
  output out_3
);

  Clock clock_1 (.out(in_2));
  and and_1 (out_3, in_1, in_2);
endmodule

module program_counter_16b (
  input  in_1,
  input  in_2,
  input  in_3,
  input  [15:0] load_input,
  output out_5,
  output [15:0] out_6
);

  Counter #(.max('hffff), .width(16)) counter_1 (
    .clr(in_1), .load(in_2), .clk(in_3), .D(load_input), .carry(out_5), .Q(out_6));  // open: up, count
endmodule

module sap_2 (
  output [7:0] out_1
);

  wire alu_8b_1_negative_flag, alu_8b_1_zero_flag, clock_1_out;
  wire [7:0] accumulator_out_6, B_out_6, bit_expander_16_8_1_out_3, bit_expander_16_8_2_out_3,
       bit_expander_16_8_3_out_3, bit_expander_16_8_4_out_3, bit_expander_16_8_5_out_3,
       bit_expander_16_8_6_out_3, C_out_6, instruction_register_out_6, memory_data_register_out_6, ram_out_6,
       tmp_out_6;
  wire [15:0] memory_address_register_out_6, program_counter_out_6, undriven;
  wire [63:0] controller_sequencer_1_out_4;

  Clock clock_1 (.out(clock_1_out));
  bit_expander_16_8 bit_expander_16_8_1 (
    .in_2(program_counter_out_6), .in_1(controller_sequencer_1_out_4[20]), .out_3(bit_expander_16_8_1_out_3));
  program_counter_16b program_counter (
    .in_3(clock_1_out), .in_1(controller_sequencer_1_out_4[23]), .in_2(controller_sequencer_1_out_4[24]),
    .load_input(undriven), .out_6(program_counter_out_6));  // open: out_5
  register_16b memory_address_register (
    .in_1(controller_sequencer_1_out_4[13]), .in_2(program_counter_out_6),
    .in_3(controller_sequencer_1_out_4[12]), .in_4(clock_1_out), .in_5(controller_sequencer_1_out_4[14]),
    .out_6(memory_address_register_out_6));
  memory_64k_8b ram (
    .in_5(bit_expander_16_8_2_out_3), .in_1(memory_address_register_out_6),
    .in_2(controller_sequencer_1_out_4[15]), .in_3(controller_sequencer_1_out_4[16]), .in_4(clock_1_out),
    .out_6(ram_out_6));
  register_8b memory_data_register (
    .in_1(controller_sequencer_1_out_4[18]), .in_2(ram_out_6), .in_3(controller_sequencer_1_out_4[17]),
    .in_4(clock_1_out), .in_5(controller_sequencer_1_out_4[19]), .out_6(memory_data_register_out_6));
  register_8b instruction_register (
    .in_1(controller_sequencer_1_out_4[21]), .in_2(bit_expander_16_8_1_out_3),
    .in_3(controller_sequencer_1_out_4[20]), .in_4(clock_1_out), .in_5(controller_sequencer_1_out_4[22]),
    .out_6(instruction_register_out_6));
  controller_sequencer controller_sequencer_1 (
    .pc(program_counter_out_6), .controller_in(instruction_register_out_6), .clk(clock_1_out),
    .out_4(controller_sequencer_1_out_4));
  assign program_counter_out_6 = controller_sequencer_1_out_4[24] ? undriven : 16'bz;  // Controlled_Buffer controlled_buffer_1
  bit_expander_8_by_16 bit_expander_8_by_16_1 (
    .in_2(memory_data_register_out_6), .in_1(controller_sequencer_1_out_4[18]), .out_3(program_counter_out_6));
  bit_expander_16_8 bit_expander_16_8_2 (
    .in_2(program_counter_out_6), .in_1(controller_sequencer_1_out_4[15]), .out_3(bit_expander_16_8_2_out_3));
  bit_expander_16_8 bit_expander_16_8_3 (
    .in_2(program_counter_out_6), .in_1(controller_sequencer_1_out_4[0]), .out_3(bit_expander_16_8_3_out_3));
  bit_expander_16_8 bit_expander_16_8_4 (
    .in_2(program_counter_out_6), .in_1(controller_sequencer_1_out_4[3]), .out_3(bit_expander_16_8_4_out_3));
  bit_expander_16_8 bit_expander_16_8_5 (
    .in_2(program_counter_out_6), .in_1(controller_sequencer_1_out_4[6]), .out_3(bit_expander_16_8_5_out_3));
  bit_expander_16_8 bit_expander_16_8_6 (
    .in_2(program_counter_out_6), .in_1(controller_sequencer_1_out_4[9]), .out_3(bit_expander_16_8_6_out_3));
  register_8b accumulator (
    .in_1(controller_sequencer_1_out_4[1]), .in_2(bit_expander_16_8_3_out_3),
    .in_3(controller_sequencer_1_out_4[0]), .in_4(clock_1_out), .in_5(controller_sequencer_1_out_4[2]),
    .out_6(accumulator_out_6));
  alu_8b alu_8b_1 (
    .Acc(accumulator_out_6), .Tmp(tmp_out_6), .alu_op(controller_sequencer_1_out_4[34:25]),
    .negative_flag(alu_8b_1_negative_flag), .zero_flag(alu_8b_1_zero_flag), .out_4(out_1));
  register_8b tmp (
    .in_1(controller_sequencer_1_out_4[4]), .in_2(bit_expander_16_8_4_out_3),
    .in_3(controller_sequencer_1_out_4[3]), .in_4(clock_1_out), .in_5(controller_sequencer_1_out_4[5]),
    .out_6(tmp_out_6));
  register_8b B (
    .in_1(controller_sequencer_1_out_4[7]), .in_2(bit_expander_16_8_5_out_3),
    .in_3(controller_sequencer_1_out_4[6]), .in_4(clock_1_out), .in_5(controller_sequencer_1_out_4[8]),
    .out_6(B_out_6));
  register_8b C (
    .in_1(controller_sequencer_1_out_4[10]), .in_2(bit_expander_16_8_6_out_3),
    .in_3(controller_sequencer_1_out_4[9]), .in_4(clock_1_out), .in_5(controller_sequencer_1_out_4[11]),
    .out_6(C_out_6));
  bit_expander_8_by_16 bit_expander_8_by_16_2 (
    .in_2(accumulator_out_6), .in_1(controller_sequencer_1_out_4[1]), .out_3(program_counter_out_6));
  bit_expander_8_by_16 bit_expander_8_by_16_3 (
    .in_2(tmp_out_6), .in_1(controller_sequencer_1_out_4[4]), .out_3(program_counter_out_6));
  bit_expander_8_by_16 bit_expander_8_by_16_4 (
    .in_2(B_out_6), .in_1(controller_sequencer_1_out_4[7]), .out_3(program_counter_out_6));
  bit_expander_8_by_16 bit_expander_8_by_16_5 (
    .in_2(C_out_6), .in_1(controller_sequencer_1_out_4[10]), .out_3(program_counter_out_6));
endmodule

module register_16b (
  input  in_1,
  input  [15:0] in_2,
  input  in_3,
  input  in_4,
  input  in_5,
  output [15:0] out_6
);

  wire [15:0] register_1_q;

  Register #(.width(16)) register_1 (.D(in_2), .en(in_3), .clk(in_4), .Q(register_1_q), .clr(in_5));
  assign out_6 = in_1 ? register_1_q : 16'bz;  // Controlled_Buffer controlled_buffer_1
endmodule

module memory_64k_8b (
  input  [15:0] in_1,
  input  in_2,
  input  in_3,
  input  in_4,
  input  [7:0] in_5,
  output [7:0] out_6
);

  RAM #(.addrWidth(16), .\type ("nonvolatile")) ram_1 (
    .addr(in_1), .we(in_2), .oe(in_3), .clk(in_4), .din(in_5), .dout(out_6));
endmodule

module register_8b (
  input  in_1,
  input  [7:0] in_2,
  input  in_3,
  input  in_4,
  input  in_5,
  output [7:0] out_6
);

  wire [7:0] register_1_q;

  Register register_1 (.D(in_2), .en(in_3), .clk(in_4), .Q(register_1_q), .clr(in_5));
  assign out_6 = in_1 ? register_1_q : 8'bz;  // Controlled_Buffer controlled_buffer_1
endmodule

module alu_8b (
  input  [9:0] alu_op,
  input  [7:0] Acc,
  input  [7:0] Tmp,
  output [7:0] out_4,
  output negative_flag,
  output zero_flag
);

  wire or_1_out, or_2_out, undriven;
  wire [7:0] and_1_out, controlled_buffer_1_out, controlled_buffer_4_out, not_1_out, not_2_out, or_3_out,
       shifter_1_out, shifter_2_out, xor_1_out;

  assign controlled_buffer_1_out = alu_op[2] ? Tmp : 8'bz;  // Controlled_Buffer controlled_buffer_1
  or or_1 (or_1_out, alu_op[0], alu_op[1]);
  assign controlled_buffer_1_out = or_1_out ? Acc : 8'bz;  // Controlled_Buffer controlled_buffer_2
  assign controlled_buffer_1_out = alu_op[3] ? 8'h1 : 8'bz;  // Controlled_Buffer controlled_buffer_3
  assign not_1_out = ~Tmp;  // NOT_Gate not_1, 8 bits wide
  assign not_2_out = ~8'h1;  // NOT_Gate not_2, 8 bits wide
  assign controlled_buffer_4_out = alu_op[1] ? not_1_out : 8'bz;  // Controlled_Buffer controlled_buffer_4
  assign controlled_buffer_4_out = alu_op[0] ? Tmp : 8'bz;  // Controlled_Buffer controlled_buffer_5
  assign controlled_buffer_4_out = alu_op[3] ? Tmp : 8'bz;  // Controlled_Buffer controlled_buffer_6
  assign controlled_buffer_4_out = alu_op[2] ? not_2_out : 8'bz;  // Controlled_Buffer controlled_buffer_7
  Shifter #(.shift("rr")) shifter_1 (.in(Tmp), .\dist (3'b001), .out(shifter_1_out));
  or or_2 (or_2_out, alu_op[2], alu_op[1]);
  Adder adder_1 (
    .a(controlled_buffer_1_out), .b(controlled_buffer_4_out), .out({negative_flag, out_4[6:0]}),
    .cin(or_2_out));  // open: cout
  assign {negative_flag, out_4[6:0]} = alu_op[7] ? shifter_2_out : 8'bz;  // Controlled_Buffer controlled_buffer_8
  Shifter #(.shift("rl")) shifter_2 (.in(Tmp), .\dist (3'b001), .out(shifter_2_out));
  assign {negative_flag, out_4[6:0]} = alu_op[8] ? shifter_1_out : 8'bz;  // Controlled_Buffer controlled_buffer_9
  assign and_1_out = Acc & Tmp;  // AND_Gate and_1, 8 bits wide
  assign xor_1_out = Acc ^ Tmp;  // XOR_Gate xor_1, 8 bits wide
  assign {negative_flag, out_4[6:0]} = alu_op[6] ? xor_1_out : 8'bz;  // Controlled_Buffer controlled_buffer_10
  assign or_3_out = Acc | Tmp;  // OR_Gate or_3, 8 bits wide
  assign {negative_flag, out_4[6:0]} = alu_op[5] ? or_3_out : 8'bz;  // Controlled_Buffer controlled_buffer_11
  assign {negative_flag, out_4[6:0]} = alu_op[4] ? and_1_out : 8'bz;  // Controlled_Buffer controlled_buffer_12
  assign {negative_flag, out_4[6:0]} = undriven ? not_1_out : 8'bz;  // Controlled_Buffer controlled_buffer_13
  nor nor_1 (zero_flag, negative_flag, out_4[6], out_4[5], out_4[4], out_4[3], out_4[2], out_4[1], out_4[0]);

  assign out_4[7] = negative_flag;

  // Notes on the sheet:
  //   dcr
  //   inr
  //   and
  //   add
  //   sub
endmodule

module bit_expander_8_by_16 (
  input  in_1,
  input  [7:0] in_2,
  output [15:0] out_3
);

  assign out_3 = in_1 ? {{8{1'b0}}, in_2} : 16'bz;  // Controlled_Buffer controlled_buffer_1
endmodule

module bit_expander_16_8 (
  input  in_1,
  input  [15:0] in_2,
  output [7:0] out_3
);

  assign out_3 = in_1 ? in_2[7:0] : 8'bz;  // Controlled_Buffer controlled_buffer_1
endmodule

module controller_sequencer (
  input  [7:0] controller_in,
  input  clk,
  input  [15:0] pc,
  output [63:0] out_4
);

  wire and_1_out, and_2_out, controlled_buffer_1_out, controlled_buffer_2_out;
  wire [7:0] counter_1_q, rom_1_data;

  ROM rom_1 (.addr(controller_in), .data(rom_1_data));
  and and_1 (and_1_out, pc[0], pc[1], ~pc[2], ~pc[3], ~pc[4], ~pc[5], ~pc[6], ~pc[7], ~pc[8], ~pc[9], ~pc[10], ~pc[11], ~pc[12], ~pc[13], ~pc[14], ~pc[15]);  // AND_Gate
  and and_2 (and_2_out, ~pc[0], ~pc[1], ~pc[2], ~pc[3], ~pc[4], ~pc[5], ~pc[6], ~pc[7], ~pc[8], ~pc[9], ~pc[10], ~pc[11], ~pc[12], ~pc[13], ~pc[14], ~pc[15]);  // AND_Gate
  assign controlled_buffer_1_out = clk ? and_1_out : 1'bz;  // Controlled_Buffer controlled_buffer_1
  assign controlled_buffer_2_out = clk ? and_2_out : 1'bz;  // Controlled_Buffer controlled_buffer_2
  Counter counter_1 (
    .clr(controlled_buffer_2_out), .load(controlled_buffer_1_out), .clk(clk), .D(rom_1_data), .Q(counter_1_q));  // open: up, count, carry
  ROM #(.dataWidth(64)) rom_2 (.addr(counter_1_q), .data(out_4));

  // Notes on the sheet:
  //   contents of rom_1 (hex, n*v repeats v):
  //   4*0 2
  //   contents of rom_2 (hex, n*v repeats v):
  //   7*0 333 21*0 100 28*0 1
endmodule
